// Digital circuit CPU 4.dig as structural Verilog
module CPU_4 (
  input  Clock,
  input  nWAIT,
  input  RST,
  input  in_6,
  output CLK1,
  output CLK2
);

  wire _74181_1_p21, _74181_1_p22, _74245_1_p13, _74245_1_p14, _74245_1_p15, _74245_1_p16, ALU_M, and_1_out,
       and_2_out, and_3_out, bussplitter_1_d1, bussplitter_1_d2, bussplitter_1_d3, C_en, COND_RES,
       demultiplexer_1_out_0, demultiplexer_1_out_1, demultiplexer_2_out_1, demultiplexer_2_out_2,
       demultiplexer_2_out_3, demultiplexer_2_out_4, demultiplexer_2_out_5, demultiplexer_2_out_6,
       demultiplexer_2_out_7, demultiplexer_3_out_0, demultiplexer_3_out_1, demultiplexer_3_out_2,
       demultiplexer_3_out_3, demultiplexer_3_out_4, demultiplexer_3_out_5, demultiplexer_3_out_6,
       demultiplexer_4_out_1, demultiplexer_4_out_2, demultiplexer_4_out_3, demultiplexer_5_out_0,
       demultiplexer_5_out_1, E_en, F_DATin, IRQ_en, MEM_dir, MEM_en, nALU_DATout, nC_st, nE_st, nIR_st,
       nMAR_ADSout, nMARH_st, nMARL_st, nMEM_DATout, nMEM_st, nOP1_st, nOP2_st, nOPS_st, not_1_out,
       not_2_out, not_3_out, not_4_out, not_26_out, not_27_out, not_28_out, not_29_out, not_30_out,
       not_31_out, nPC_ADSout, nPC_en, nPCH_st, nPCL_st, nRAR_st, nREG_DATout, nREG_st, nSEQ_en, nSEQ_st,
       or_1_out, PCL_ovf, pulldown_7_out, t_ff_1_nq, t_ff_1_q;
  wire [2:0] DOUT_sel;
  wire [3:0] _74181_1_p17, ALU_E, MEMDATA_in, multiplexer_2_out, multiplexer_3_out, nALU_c, OP1_q, OP2_q,
       OPS_q, RAR_q, REG__16x4_d, ST_sel, \µSEQ_out ;
  wire [3:3] undriven;
  wire [7:0] ADDRESS, MARL_q, PCL_out;
  wire [8:4] IR_q;
  wire [11:4] IR_q_2;
  wire [15:0] DATA;
  wire [15:4] PCH_out, PCL_out_2;
  wire [23:0] mCode_d;
  wire [23:8] CTRL_q;

  and and_1 (and_1_out, nSEQ_st, not_1_out);
  not not_1 (not_1_out, COND_RES);
  and and_2 (and_2_out, ~nALU_c[0], C_en);  // And
  and and_3 (and_3_out, ALU_E[0], E_en);
  Register #(.Bits(4)) RAR (.D(DATA[3:0]), .C(CLK2), .en(~nRAR_st), .Q(RAR_q));
  or or_1 (or_1_out, and_2_out, and_3_out);
  Register #(.Bits(4)) OP1 (.D(DATA[3:0]), .C(CLK2), .en(~nOP1_st), .Q(OP1_q));
  Register #(.Bits(4)) OP2 (.D(DATA[3:0]), .C(CLK2), .en(~nOP2_st), .Q(OP2_q));
  Register #(.Bits(4)) OPS (.D(DATA[3:0]), .C(CLK2), .en(~nOP2_st), .Q(OPS_q));
  Register #(.Bits(4)) MARH (.D(DATA[3:0]), .C(CLK2), .en(~nMARH_st), .Q(MARL_q[7:4]));
  Register #(.Bits(4)) MARL (.D(DATA[3:0]), .C(CLK2), .en(~nMARL_st), .Q(MARL_q[3:0]));
  RAMDualPort #(.AddrBits(4), .Bits(4)) REG__16x4 (
    .A(RAR_q), .Din(DATA[3:0]), .str(not_2_out), .C(CLK2), .ld(not_3_out), .D(REG__16x4_d));
  not not_2 (not_2_out, nREG_st);
  not not_3 (not_3_out, 1'b0);
  not not_4 (not_4_out, or_1_out);
  CounterPreset #(.Bits(4)) \u_µSEQ  (
    .en(~nSEQ_en), .C(CLK2), .dir(1'b0), .in({undriven[3], 3'b000}), .ld(~and_1_out), .clr(1'b0),
    .out(\µSEQ_out ));  // open: ovf
  Register RESET (.D(RST), .C(CLK2), .en(~IRQ_en), .Q(IR_q[4]));
  Register #(.Bits(12)) IR (.D(DATA[11:0]), .C(CLK2), .en(~nIR_st), .Q({IR_q_2, IR_q[8:5]}));
  Multiplexer multiplexer_1 (.in_0(or_1_out), .in_1(not_4_out), .out(COND_RES));  // open: sel
  assign ADDRESS = ~nMAR_ADSout ? MARL_q : 8'bz;  // DriverInvSel driverinvsel_1
  assign DATA[3:0] = ~nREG_DATout ? REG__16x4_d : 4'bz;  // DriverInvSel driverinvsel_2
  ROM #(.AddrBits(9), .Bits(24)) mCode (.A({IR_q, \µSEQ_out }), .sel(1'b1), .D(mCode_d));
  PullDown #(.Bits(8)) pulldown_1 (.out(ADDRESS));
  PullDown #(.Bits(4)) pulldown_2 (.out(DATA[3:0]));
  Demultiplexer demultiplexer_1 (
    .sel(ST_sel[3]), .in(1'b1), .out_0(demultiplexer_1_out_0), .out_1(demultiplexer_1_out_1));
  // _74181 _74181_1: pin names not known; wires that end beside it: nALU_c, OP1_q[0], OP1_q[1], OP1_q[2], OP1_q[3], OP2_q[0], OP2_q[1], OP2_q[2], OP2_q[3], OPS_q[0], OPS_q[1], OPS_q[2], OPS_q[3], ALU_M, 1'b1, 1'b0, _74181_1_p17[0], _74181_1_p17[1], _74181_1_p17[2], _74181_1_p17[3], _74181_1_p21, _74181_1_p22
  D_FF #(.Bits(24)) CTRL (
    .D(mCode_d), .C(CLK1), .Q({CTRL_q[23:13], MEM_en, MEM_dir, F_DATin, CTRL_q[9:8], ALU_M, DOUT_sel, ST_sel}));  // open: nQ
  Demultiplexer #(.Selector_Bits(3)) demultiplexer_2 (
    .sel(ST_sel[2:0]), .in(demultiplexer_1_out_0), .out_1(demultiplexer_2_out_1),
    .out_2(demultiplexer_2_out_2), .out_3(demultiplexer_2_out_3), .out_4(demultiplexer_2_out_4),
    .out_5(demultiplexer_2_out_5), .out_6(demultiplexer_2_out_6), .out_7(demultiplexer_2_out_7));  // open: out_0
  Demultiplexer #(.Selector_Bits(3)) demultiplexer_3 (
    .sel(ST_sel[2:0]), .in(demultiplexer_1_out_1), .out_0(demultiplexer_3_out_0),
    .out_1(demultiplexer_3_out_1), .out_2(demultiplexer_3_out_2), .out_3(demultiplexer_3_out_3),
    .out_4(demultiplexer_3_out_4), .out_5(demultiplexer_3_out_5), .out_6(demultiplexer_3_out_6));  // open: out_7
  CounterPreset #(.Bits(16)) PCH (
    .en(~PCL_ovf), .C(CLK2), .dir(1'b0), .in(DATA), .ld(~nPCH_st), .clr(1'b0), .out({PCH_out, PCL_out[7:4]}));  // open: ovf
  CounterPreset #(.Bits(16)) PCL (
    .en(~nPC_en), .C(CLK2), .dir(1'b0), .in(DATA), .ld(~nPCL_st), .clr(1'b0),
    .out({PCL_out_2, PCL_out[3:0]}), .ovf(PCL_ovf));
  not not_5 (nPC_ADSout, CTRL_q[8]);
  not not_6 (nMAR_ADSout, CTRL_q[9]);
  not not_7 (nSEQ_en, CTRL_q[14]);
  not not_8 (nPC_en, CTRL_q[15]);
  not not_9 (nOP1_st, demultiplexer_2_out_1);
  not not_10 (nOP2_st, demultiplexer_2_out_2);
  not not_11 (nOPS_st, demultiplexer_2_out_3);
  not not_12 (nREG_st, demultiplexer_2_out_4);
  not not_13 (nPCL_st, demultiplexer_2_out_5);
  not not_14 (nPCH_st, demultiplexer_2_out_6);
  not not_15 (nMEM_st, demultiplexer_2_out_7);
  not not_16 (nMARL_st, demultiplexer_3_out_0);
  not not_17 (nMARH_st, demultiplexer_3_out_1);
  not not_18 (nRAR_st, demultiplexer_3_out_2);
  not not_19 (nIR_st, demultiplexer_3_out_3);
  not not_20 (nE_st, demultiplexer_3_out_4);
  not not_21 (nC_st, demultiplexer_3_out_5);
  not not_22 (nSEQ_st, demultiplexer_3_out_6);
  Multiplexer multiplexer_2 (.sel(F_DATin), .in_0(_74181_1_p21), .in_1(DATA[0]), .out(multiplexer_2_out[0]));
  Multiplexer multiplexer_3 (.sel(F_DATin), .in_0(_74181_1_p22), .in_1(DATA[0]), .out(multiplexer_3_out[0]));
  assign ADDRESS = ~nPC_ADSout ? PCL_out : 8'bz;  // DriverInvSel driverinvsel_3
  Demultiplexer #(.Selector_Bits(3)) demultiplexer_4 (
    .sel(DOUT_sel), .in(1'b1), .out_1(demultiplexer_4_out_1), .out_2(demultiplexer_4_out_2),
    .out_3(demultiplexer_4_out_3), .out_6(C_en), .out_7(E_en));  // open: out_0, out_4, out_5
  not not_23 (nREG_DATout, demultiplexer_4_out_1);
  not not_24 (nALU_DATout, demultiplexer_4_out_2);
  not not_25 (nMEM_DATout, demultiplexer_4_out_3);
  PullDown #(.Bits(8)) pulldown_3 (.out(ADDRESS));
  not not_26 (not_26_out, Clock);
  PullDown pulldown_4 (.out(Clock));
  T_FF #(.withEnable("false")) t_ff_1 (.C(not_26_out), .Q(t_ff_1_q), .nQ(t_ff_1_nq));
  Register #(.Bits(4)) E (.D(multiplexer_2_out), .C(CLK2), .en(~nE_st), .Q(ALU_E));
  Register #(.Bits(4)) C (.D(multiplexer_3_out), .C(CLK2), .en(~nC_st), .Q(nALU_c));
  assign DATA[3:0] = ~nALU_DATout ? _74181_1_p17 : 4'bz;  // DriverInvSel driverinvsel_4
  PullDown #(.Bits(4)) pulldown_5 (.out(DATA[3:0]));
  and and_4 (CLK1, Clock, t_ff_1_q);
  and and_5 (CLK2, t_ff_1_nq, ~nWAIT, Clock);  // And
  not not_27 (not_27_out, MEM_en);
  Demultiplexer demultiplexer_5 (
    .sel(ADDRESS[7]), .in(not_27_out), .out_0(demultiplexer_5_out_0), .out_1(demultiplexer_5_out_1));
  not not_28 (not_28_out, demultiplexer_5_out_0);
  not not_29 (not_29_out, demultiplexer_5_out_1);
  not not_30 (not_30_out, not_28_out);
  ROM #(.AddrBits(8), .Bits(4)) ROM (.A(ADDRESS), .sel(not_30_out), .D(MEMDATA_in));
  RAMSinglePortSel #(.AddrBits(8), .Bits(4)) RAM (
    .A(ADDRESS), .CS(~not_29_out), .WE(~nMEM_st), .OE(~nMEM_DATout), .D(MEMDATA_in));
  PullDown #(.Bits(4)) pulldown_6 (.out(MEMDATA_in));
  PullDown pulldown_7 (.out(pulldown_7_out));
  BusSplitter #(.Bits(4)) bussplitter_1 (
    .D(MEMDATA_in), .OE(MEM_dir), .D0(pulldown_7_out), .D1(bussplitter_1_d1), .D2(bussplitter_1_d2),
    .D3(bussplitter_1_d3));
  PullDown pulldown_8 (.out(bussplitter_1_d1));
  PullDown pulldown_9 (.out(bussplitter_1_d2));
  PullDown pulldown_10 (.out(bussplitter_1_d3));
  // _74245 _74245_1: pin names not known; wires that end beside it: MEM_dir, 1'b1, 1'b0, pulldown_7_out, bussplitter_1_d1, bussplitter_1_d2, bussplitter_1_d3, 1'b0, 1'b0, 1'b0, 1'b0, MEM_en, _74245_1_p13, _74245_1_p14, _74245_1_p15, _74245_1_p16, 1'b0, 1'b0, 1'b0, 1'b0
  PullDown pulldown_11 (.out(_74245_1_p16));
  PullDown pulldown_12 (.out(_74245_1_p15));
  PullDown pulldown_13 (.out(_74245_1_p14));
  PullDown pulldown_14 (.out(_74245_1_p13));
  not not_31 (not_31_out, MEM_dir);
  BusSplitter #(.Bits(4)) bussplitter_2 (
    .D(DATA[3:0]), .OE(not_31_out), .D0(_74245_1_p13), .D1(_74245_1_p14), .D2(_74245_1_p15), .D3(_74245_1_p16));
  // Pins of 1 and 4 and 16 bits meet at DATA
  // Pins of 3 and 4 bits meet at ST_sel
  // Pins of 1 and 4 bits meet at multiplexer_2_out
  // Pins of 1 and 4 bits meet at ALU_E
  // Pins of 1 and 4 bits meet at multiplexer_3_out
  // Pins of 1 and 4 bits meet at nALU_c
  // Pins of 16 and 24 bits meet at {CTRL_q[23:13], MEM_en, MEM_dir, F_DATin, CTRL_q[9:8], ALU_M, DOUT_sel, ST_sel}
  // Pins of 4 and 16 bits meet at {PCH_out, PCL_out[7:4]}
  // Pins of 4 and 16 bits meet at {PCL_out_2, PCL_out[3:0]}
  // Pins of 3 and 4 bits meet at {undriven[3], 3'b000}
  // Pins of 4 and 12 bits meet at {IR_q_2, IR_q[8:5]}

  // Other names for the same wires on the sheet: CLK_1 = CLK1; CLK_2 = CLK2; IRQ_REQ = in_6

  // Notes on the sheet:
  //   Clock: Hz: 20
  //   CTRL
  //   ALU/REG
  //   MEM/IO
  //   contents of ROM (hex, n*v repeats v):
  //   56006*0,5,1321*0,16*45,40,48,4d,dea8,40,45,4d,dea8,40,4c,4d,dea8
  //   ,40,4c,4d,dea8,40,4f,4d,dea8,40,2c,4d,dea8,40,20,4d,dea8,40,57
  //   ,4d,dea8,40,4f,4d,dea8,40,52,4d,dea8,40,4c,4d,dea8,40,44,4d,dea8
  //   ,40,21,4d,dea8,1,8138*0,e000
endmodule
